# Fritzing sketch bouton-LED_strip (saved by Fritzing 0.9.3b)
circuit board: 8.46667cm x 5.64444cm
stripboards: 1

parts:
  Raspberry_Pi_2 = Raspberry Pi 3 [part_number=RPI-3-V1.2]
  S5 = Pushbutton [part_number="Power button" package="[THT]"]
  S6 = Round Pushbutton [part_number="Recording button"]
  LED2 = LED - 5mm [color="Red (633nm)" package="5 mm [THT]"]
  R5 = Resistor [tolerance=±5% resistance=100 package=THT]
  R6 = Resistor [tolerance=±5% resistance=1k package=THT]
  R7 = Resistor [tolerance=±5% resistance=1k package=THT]
  R8 = Resistor [tolerance=±5% resistance=10k package=THT]

nets:
  3V3: Raspberry_Pi_2.3v3, Raspberry_Pi_2.3V3, S6.leg0, R8.Pin_0
  N1: Raspberry_Pi_2.GND, S5.Pin_3, S5.Pin_4, LED2.cathode
  N2: Raspberry_Pi_2.GPIO17, R7.Pin_0
  N3: Raspberry_Pi_2.GPIO15, R5.Pin_1
  N4: Raspberry_Pi_2.GPIO14, R6.Pin_1
  N5: S5.Pin_1, S5.Pin_2, R7.Pin_1, R8.Pin_1
  N6: S6.leg1, R5.Pin_0
  N7: LED2.anode, R6.Pin_0
